# Fritzing sketch tiny_pps_proto1 (saved by Fritzing 0.9.3b)

parts:
  Mod1 = Raspberry Pi Pico
  S_L = Pushbutton [package="[THT]"]
  S_C = Pushbutton [package="[THT]"]
  S_R = Pushbutton [package="[THT]"]
  Grove1 = Grove OLED 128x96
  Grove2 = Grove 3 Axis Digital Accelerometer 16g
  C1 = Electrolytic Capacitor [capacitance=235µF voltage=32V package="100 mil [THT, electrolytic]"]
  IRFZ44N = Basic FET N-Channel [package="DPak [SMD]"]
  V- = BANANA_CONN [package=banana_conn]
  V+ = BANANA_CONN [package=banana_conn]

nets:
  N1: Mod1.pin_21, IRFZ44N.Gate
  N2: Mod1.pin_23, Mod1.pin_28, Mod1.pin_33, S_L.Pin_1, S_C.Pin_1, S_R.Pin_1, S_R.Pin_2, Grove1.GND, Grove2.GND#0
  N3: Mod1.pin_24, S_R.Pin_4
  N4: Mod1.pin_25, S_C.Pin_4
  N5: Mod1.pin_26, Grove1.SDA
  N6: Mod1.pin_27, Grove1.SCL
  N7: Mod1.pin_29, S_L.Pin_4
  N8: Mod1.pin_31, Grove2.SDA
  N9: Mod1.pin_32, Grove2.SCL
  N10: Mod1.pin_36, Grove1.VCC
  N11: Mod1.pin_39, Grove2.VCC
  N12: Grove2.VBUS, C1.+, V+.1
  N13: Grove2.GND#5, IRFZ44N.source
  N14: C1.-, IRFZ44N.drain, V-.1

custom parts:
  Raspberry Pi Pico: Raspberry Pi Pico. Based around the RP2040 microcontroller the Pico is a low cost microcontroller device bringing Raspberry Pi quality, cost, and easy of use to the microcontroller space. Jan 2021, Split part in to two versions: tht (this one) and SMD. This one will drill holes for a .1 in header in pcb to allow plugging in the module as well as providing pads to solder the module to the top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
  Grove 3 Axis Digital Accelerometer 16g: A 3 axis digital accelerometer (16g)
